# Fritzing sketch Garage (saved by Fritzing 0.9.3b)
circuit board: 8.46667cm x 5.64444cm

parts:
  Part1 = Arduino Nano (Rev3.0)
  Part2 = NRF24L01+ Breakout Board
  KY-1 = Keyes Relay [package=THT]
  S1 = Reed switch [package=THT]
  S2 = Reed switch [package=THT]

nets:
  GND: Part1.GND, Part2.GND, KY-1.ground, S1.pin_2, S2.pin_2
  N1: Part1.D2, Part2.IRQ
  N2: Part1.D3, KY-1.signal
  N3: Part1.D7, S2.pin_1
  N4: Part1.D8, S1.pin_1
  N5: Part1.D9, Part2.CE
  N6: Part1.D10, Part2.CS
  N7: Part1.D11/MOSI, Part2.MOSI
  N8: Part1.D12/MISO, Part2.MISO
  N9: Part1.5V, KY-1.power
  3V3: Part1.3V3, Part2.VCC
  N10: Part1.D13/SCK, Part2.SCK

custom parts:
  Keyes Relay: The Keyes 5V relay module is suitable for SCM development, home appliance control. It uses a 5V~12V TIL control signal which can control DC / AC signal.
