# Fritzing sketch TempHumSensor (saved by Fritzing 0.9.3b)

parts:
  Part1 = Arduino Nano (Rev3.0)
  DHT1 = DHT22 Humidity and Temperature Sensor
  Part2 = NRF24L01+ Breakout Board

nets:
  GND: Part1.GND, DHT1.GND, Part2.GND
  N1: Part1.D2, Part2.IRQ
  N2: Part1.D3, DHT1.DATA
  N3: Part1.D9, Part2.CE
  N4: Part1.D10, Part2.CS
  N5: Part1.D11/MOSI, Part2.MOSI
  N6: Part1.D12/MISO, Part2.MISO
  5V: Part1.5V, DHT1.VDD
  3V3: Part1.3V3, Part2.VCC
  N7: Part1.D13/SCK, Part2.SCK
