# Fritzing sketch Kitchen (saved by Fritzing 0.9.3b)
breadboards: 1

parts:
  Part1 = Arduino Nano (Rev3.0)
  Part2 = NRF24L01+ Breakout Board
  U1 = FS1000A - 433Mhz RF Transmitter [package=THT]
  hc-sr1 = hc-sr04
  DHT1 = DHT22 Humidity and Temperature Sensor

nets:
  GND: Part1.GND, Part2.GND, U1.GND, hc-sr1.GND, DHT1.GND
  N1: Part1.D2, Part2.IRQ
  N2: Part1.D4, DHT1.DATA
  N3: Part1.D5, U1.DATA
  N4: Part1.D6, hc-sr1.Echo
  N5: Part1.D7, hc-sr1.Trig
  N6: Part1.D9, Part2.CE
  N7: Part1.D10, Part2.CS
  N8: Part1.D11/MOSI, Part2.MOSI
  N9: Part1.D12/MISO, Part2.MISO
  VCC: Part1.5V, U1.VCC, hc-sr1.VCC, DHT1.VDD
  3V3: Part1.3V3, Part2.VCC
  N10: Part1.D13/SCK, Part2.SCK

custom parts:
  FS1000A - 433Mhz RF Transmitter: This is 433Mhz RF transmitter with receiver kit for Arduino ARM MCU wireless Application environment: Remote control switch, receiver module, motorcycles, automobile anti-theft products, home security products, electric doors, shutter doors, windows, remote control socket, remote control LED, remote audio remote control electric doors, garage door remote control, remote control retractable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
